// Logisim project 250 Proj v2.circ as structural Verilog: 10 circuits, main circuit Clock
module Clock (
  input  Reset,
  input  Start
);

  wire and_1_out, clock_1_out, clock_2_out, days_1_out_4, hrs_1_out_4, mins_1_out_4, months_1_out_4,
       sec_1_out_4, stop_mins_1_out_5, stop_secs_1_out_5;
  wire [3:0] days_1_out_2, days_1_out_3, hrs_1_out_2, hrs_1_out_3, mins_1_out_2, mins_1_out_3,
       months_1_out_2, months_1_out_3, sec_1_out_2, sec_1_out_3, stop_hrs_1_out_3, stop_hrs_1_out_4,
       stop_mins_1_out_3, stop_mins_1_out_4, stop_secs_1_out_3, stop_secs_1_out_4, years_1_out_2,
       years_1_out_3, years_1_out_4, years_1_out_5;

  Hex_Digit_Display hex_digit_display_1 (.value(hrs_1_out_3));  // open: dp
  Hex_Digit_Display hex_digit_display_2 (.value(hrs_1_out_2));  // open: dp
  Hrs hrs_1 (.in_1(mins_1_out_4), .out_2(hrs_1_out_2), .out_3(hrs_1_out_3), .out_4(hrs_1_out_4));
  Hex_Digit_Display hex_digit_display_3 (.value(stop_hrs_1_out_3));  // open: dp
  Hex_Digit_Display hex_digit_display_4 (.value(stop_hrs_1_out_4));  // open: dp
  Stop_Hrs stop_hrs_1 (.in_1(stop_mins_1_out_5), .out_3(stop_hrs_1_out_3), .out_4(stop_hrs_1_out_4), .in_2(Reset));
  Hex_Digit_Display hex_digit_display_5 (.value(mins_1_out_3));  // open: dp
  Hex_Digit_Display hex_digit_display_6 (.value(mins_1_out_2));  // open: dp
  Mins mins_1 (.in_1(sec_1_out_4), .out_2(mins_1_out_2), .out_3(mins_1_out_3), .out_4(mins_1_out_4));
  Hex_Digit_Display hex_digit_display_7 (.value(stop_mins_1_out_3));  // open: dp
  Stop_Mins stop_mins_1 (
    .in_1(stop_secs_1_out_5), .out_3(stop_mins_1_out_3), .out_4(stop_mins_1_out_4), .in_2(Reset),
    .out_5(stop_mins_1_out_5));
  Hex_Digit_Display hex_digit_display_8 (.value(sec_1_out_2));  // open: dp
  Sec sec_1 (.in_1(clock_1_out), .out_2(sec_1_out_2), .out_3(sec_1_out_3), .out_4(sec_1_out_4));
  Clock_part clock_1 (.out(clock_1_out));
  Hex_Digit_Display hex_digit_display_9 (.value(stop_mins_1_out_4));  // open: dp
  Hex_Digit_Display hex_digit_display_10 (.value(stop_secs_1_out_3));  // open: dp
  and and_1 (and_1_out, Start, clock_2_out);
  Clock_part clock_2 (.out(clock_2_out));
  Hex_Digit_Display hex_digit_display_11 (.value(sec_1_out_3));  // open: dp
  Hex_Digit_Display hex_digit_display_12 (.value(stop_secs_1_out_4));  // open: dp
  Stop_Secs stop_secs_1 (
    .in_1(and_1_out), .out_3(stop_secs_1_out_3), .out_4(stop_secs_1_out_4), .in_2(Reset),
    .out_5(stop_secs_1_out_5));
  Hex_Digit_Display hex_digit_display_13 (.value(years_1_out_2));  // open: dp
  Hex_Digit_Display hex_digit_display_14 (.value(years_1_out_3));  // open: dp
  Years years_1 (
    .out_2(years_1_out_2), .out_3(years_1_out_3), .out_4(years_1_out_4), .out_5(years_1_out_5),
    .in_1(months_1_out_4));
  Hex_Digit_Display hex_digit_display_15 (.value(years_1_out_4));  // open: dp
  Hex_Digit_Display hex_digit_display_16 (.value(years_1_out_5));  // open: dp
  Hex_Digit_Display hex_digit_display_17 (.value(months_1_out_2));  // open: dp
  Months months_1 (.in_1(days_1_out_4), .out_2(months_1_out_2), .out_3(months_1_out_3), .out_4(months_1_out_4));
  Hex_Digit_Display hex_digit_display_18 (.value(months_1_out_3));  // open: dp
  Hex_Digit_Display hex_digit_display_19 (.value(days_1_out_2));  // open: dp
  Hex_Digit_Display hex_digit_display_20 (.value(days_1_out_3));  // open: dp
  Days days_1 (.in_1(hrs_1_out_4), .out_2(days_1_out_2), .out_3(days_1_out_3), .out_4(days_1_out_4));
endmodule

module Sec (
  input  in_1,
  output [3:0] out_2,
  output [3:0] out_3,
  output out_4
);

  wire and_1_out;

  Counter #(.width(4), .max('hf)) counter_1 (.Q(out_3), .clk(in_1), .clr(and_1_out));  // open: load, D, count, carry
  and and_1 (and_1_out, out_3[1], out_3[3]);
  Counter #(.width(4), .max('hf)) counter_2 (.Q(out_2), .clk(and_1_out), .clr(out_4));  // open: load, D, count, carry
  and and_2 (out_4, out_2[2], out_2[1]);
endmodule

module Mins (
  input  in_1,
  output [3:0] out_2,
  output [3:0] out_3,
  output out_4
);

  wire and_1_out;

  Counter #(.width(4), .max('hf)) counter_1 (.Q(out_3), .clk(in_1), .clr(and_1_out));  // open: load, D, count, carry
  Counter #(.width(4), .max('hf)) counter_2 (.Q(out_2), .clk(and_1_out), .clr(out_4));  // open: load, D, count, carry
  and and_1 (and_1_out, out_3[1], out_3[3]);
  and and_2 (out_4, out_2[2], out_2[1]);
endmodule

module Hrs (
  input  in_1,
  output [3:0] out_2,
  output [3:0] out_3,
  output out_4
);

  wire and_2_out, or_1_out;

  Counter #(.width(4), .max('hf)) counter_1 (.Q(out_3), .clk(in_1), .clr(or_1_out));  // open: load, D, count, carry
  or or_1 (or_1_out, and_2_out, out_4);
  and and_1 (out_4, out_3[2], out_2[1]);
  Counter #(.width(4), .max('hf)) counter_2 (.Q(out_2), .clk(and_2_out), .clr(out_4));  // open: load, D, count, carry
  and and_2 (and_2_out, out_3[1], out_3[3]);
endmodule

module Days (
  input  in_1,
  output [3:0] out_2,
  output [3:0] out_3,
  output out_4
);

  wire and_1_out, and_2_out, not_1_out, not_2_out, or_1_out, or_2_out, or_3_out;

  not not_1 (not_1_out, or_2_out);
  and and_1 (and_1_out, not_1_out, not_2_out);
  not not_2 (not_2_out, or_3_out);
  Counter #(.width(4), .max('hf)) counter_1 (
    .load(and_1_out), .D(4'b0001), .Q(out_3), .clk(in_1), .clr(or_1_out));  // open: count, carry
  or or_1 (or_1_out, and_2_out, out_4);
  or or_2 (or_2_out, out_3[3], out_3[2], out_3[1], out_3[0]);
  Counter #(.width(4), .max('hf)) counter_2 (.Q(out_2), .clk(and_2_out), .clr(out_4));  // open: load, D, count, carry
  and and_2 (and_2_out, out_3[1], out_3[3]);
  or or_3 (or_3_out, out_2[3], out_2[2], out_2[1], out_2[0]);
  and and_3 (out_4, out_2[0], out_2[1], out_3[0]);
endmodule

module Months (
  input  in_1,
  output [3:0] out_2,
  output [3:0] out_3,
  output out_4
);

  wire _10_out, _30_out, _31_out, and_1_out, Dec_out, Jul_out, Jun_out, Mar_out, May_out, not_1_out,
       not_2_out, Nov_out, Oct_out, or_1_out, or_2_out, or_3_out, Sep_out;

  Counter #(.width(4), .max('hf)) counter_1 (
    .load(and_1_out), .D(4'b0001), .Q(out_3), .clk(in_1), .clr(or_1_out));  // open: count, carry
  or or_1 (or_1_out, _10_out, out_4);
  not not_1 (not_1_out, or_2_out);
  and and_1 (and_1_out, not_1_out, not_2_out);
  not not_2 (not_2_out, or_3_out);
  and _10 (_10_out, out_3[1], out_3[3]);
  and _13 (out_4, out_3[0], out_3[1], out_2[0]);
  or or_2 (or_2_out, out_3[3], out_3[2], out_3[1], out_3[0]);
  Counter #(.width(4), .max('hf)) counter_2 (.Q(out_2), .clk(_10_out), .clr(out_4));  // open: load, D, count, carry
  or or_3 (or_3_out, out_2[3], out_2[2], out_2[1], out_2[0]);
  or Mar (Mar_out, out_3[3], out_3[2]);
  or May (May_out, out_3[3], out_3[1]);
  or Jun (Jun_out, out_3[2], out_3[1]);
  or Jul (Jul_out, out_3[3], out_3[2], out_3[1]);
  or Sep (Sep_out, out_3[3], out_3[0]);
  or Oct (Oct_out, out_3[2], out_3[0]);
  or Nov (Nov_out, out_3[3], out_3[2], out_3[0]);
  or Dec (Dec_out, out_3[1], out_3[0]);
  or _31 (_31_out, Mar_out, May_out, Jul_out, out_3[3], Oct_out, Dec_out, out_3[0]);
  or _30 (_30_out, out_3[1], Jun_out, Sep_out, Nov_out);
endmodule

module Years (
  input  in_1,
  output [3:0] out_2,
  output [3:0] out_3,
  output [3:0] out_4,
  output [3:0] out_5
);

  wire and_1_out, and_2_out, and_3_out, and_4_out;

  Counter #(.width(4), .max('hf)) counter_1 (
    .Q(out_2), .clk(and_2_out), .clr(and_1_out));  // open: load, D, count, carry
  Counter #(.width(4), .max('hf)) counter_2 (
    .Q(out_3), .clk(and_3_out), .clr(and_2_out));  // open: load, D, count, carry
  and and_1 (and_1_out, out_2[3], out_2[1]);
  Counter #(.width(4), .max('hf)) counter_3 (
    .Q(out_4), .clk(and_4_out), .clr(and_3_out));  // open: load, D, count, carry
  and and_2 (and_2_out, out_3[3], out_3[1]);
  and and_3 (and_3_out, out_4[3], out_4[1]);
  Counter #(.width(4), .max('hf)) counter_4 (.Q(out_5), .clk(in_1), .clr(and_4_out));  // open: load, D, count, carry
  and and_4 (and_4_out, out_5[3], out_5[1]);
endmodule

module Stop_Hrs (
  input  in_1,
  input  in_2,
  output [3:0] out_3,
  output [3:0] out_4
);

  wire and_1_out, and_2_out, and_3_out, or_1_out, or_2_out;

  Counter #(.width(4), .max('hf)) counter_1 (.Q(out_4), .clk(in_1), .clr(or_1_out));  // open: load, D, count, carry
  or or_1 (or_1_out, and_1_out, or_2_out, and_2_out);
  Counter #(.width(4), .max('hf)) counter_2 (
    .Q(out_3), .clk(and_1_out), .clr(or_2_out));  // open: load, D, count, carry
  and and_1 (and_1_out, out_4[1], out_4[3]);
  and and_2 (and_2_out, and_1_out, and_3_out);
  or or_2 (or_2_out, and_2_out, in_2);
  and and_3 (and_3_out, out_3[3], out_3[0]);
endmodule

module Stop_Mins (
  input  in_1,
  input  in_2,
  output [3:0] out_3,
  output [3:0] out_4,
  output out_5
);

  wire and_1_out, or_1_out, or_2_out, or_3_out;

  Counter #(.width(4), .max('hf)) counter_1 (.Q(out_4), .clk(in_1), .clr(or_1_out));  // open: load, D, count, carry
  or or_1 (or_1_out, or_2_out, and_1_out);
  and and_1 (and_1_out, out_4[1], out_4[3]);
  or or_2 (or_2_out, out_5, in_2);
  Counter #(.width(4), .max('hf)) counter_2 (
    .Q(out_3), .clk(and_1_out), .clr(or_3_out));  // open: load, D, count, carry
  or or_3 (or_3_out, out_5, or_2_out);
  and and_2 (out_5, out_3[2], out_3[1]);
endmodule

module Stop_Secs (
  input  in_1,
  input  in_2,
  output [3:0] out_3,
  output [3:0] out_4,
  output out_5
);

  wire and_1_out, or_1_out, or_2_out, or_3_out;

  or or_1 (or_1_out, or_3_out, and_1_out);
  Counter #(.width(4), .max('hf)) counter_1 (.Q(out_4), .clk(in_1), .clr(or_1_out));  // open: load, D, count, carry
  Counter #(.width(4), .max('hf)) counter_2 (
    .Q(out_3), .clk(and_1_out), .clr(or_2_out));  // open: load, D, count, carry
  or or_2 (or_2_out, or_3_out, out_5);
  and and_1 (and_1_out, out_4[1], out_4[3]);
  or or_3 (or_3_out, out_5, in_2);
  and and_2 (out_5, out_3[2], out_3[1]);
endmodule
