// Logisim project calc logisim.circ 2.circ as structural Verilog: 2 circuits, main circuit main
module main (
  input  in_1,
  input  in_2,
  input  in_3,
  input  in_4,
  input  in_5,
  input  in_6,
  input  in_7,
  input  in_8,
  input  in_9,
  input  in_10,
  input  in_11,
  input  in_12,
  input  in_13,
  output out_14,
  output out_15,
  output out_16,
  output out_17,
  output out_18
);

  wire full_adder_2_carry_out, full_adder_3_carry_out, full_adder_4_carry_out;

  full_adder full_adder_1 (.A(in_2), .B(in_6), .Carry(full_adder_2_carry_out), .Sum(out_14), .Carry_out(out_18));
  Button _1 ();  // open: out
  Button _4 ();  // open: out
  Button _7 ();  // open: out
  full_adder full_adder_2 (
    .A(in_3), .B(in_7), .Carry(full_adder_3_carry_out), .Sum(out_15), .Carry_out(full_adder_2_carry_out));
  Button _3 ();  // open: out
  Button _2 ();  // open: out
  Button _6 ();  // open: out
  Button _5 ();  // open: out
  Button _8 ();  // open: out
  Button _9 ();  // open: out
  Button _0 ();  // open: out
  full_adder full_adder_3 (
    .A(in_4), .B(in_8), .Carry(full_adder_4_carry_out), .Sum(out_16), .Carry_out(full_adder_3_carry_out));
  full_adder full_adder_4 (.A(in_5), .B(in_9), .Carry(in_1), .Sum(out_17), .Carry_out(full_adder_4_carry_out));
endmodule

module full_adder (
  input  Carry,
  input  A,
  input  B,
  output Sum,
  output Carry_out
);

  wire and_1_out, and_2_out, xor_1_out;

  xor xor_1 (xor_1_out, A, B);
  and and_1 (and_1_out, A, B);
  xor xor_2 (Sum, Carry, xor_1_out);
  and and_2 (and_2_out, Carry, xor_1_out);
  or or_1 (Carry_out, and_2_out, and_1_out);
endmodule
