// Logisim project lab 11.circ as structural Verilog: 9 circuits, main circuit Basic Register
module Basic_Register (
  input  Clear_reset,
  input  D0,
  input  D1,
  input  D2,
  input  D3,
  output out_6,
  output out_7,
  output out_8,
  output out_9
);

  wire clock_1_out;

  Clock clock_1 (.out(clock_1_out));
  D_Flip_Flop d_ff_1 (.clk(clock_1_out), .D(D0), .Q(out_6), .reset(Clear_reset));  // open: Qn, preset, en
  D_Flip_Flop d_ff_2 (.clk(clock_1_out), .D(D1), .Q(out_7), .reset(Clear_reset));  // open: Qn, preset, en
  D_Flip_Flop d_ff_3 (.clk(clock_1_out), .D(D2), .Q(out_8), .reset(Clear_reset));  // open: Qn, preset, en
  D_Flip_Flop d_ff_4 (.clk(clock_1_out), .D(D3), .Q(out_9), .reset(Clear_reset));  // open: Qn, preset, en
  LED led_1 (.in(out_6));
  LED led_2 (.in(out_7));
  LED led_3 (.in(out_8));
  LED led_4 (.in(out_9));

  // Notes on the sheet:
  //   Clock
endmodule

module Register_with_a_Par_Load (
  input  Load,
  input  D0,
  input  D1,
  input  D2,
  input  D3,
  output out_6,
  output out_7,
  output out_8,
  output out_9
);

  wire clock_1_out, not_1_out, or_1_out;

  Clock clock_1 (.out(clock_1_out));
  not not_1 (not_1_out, Load);
  or or_1 (or_1_out, clock_1_out, not_1_out);
  D_Flip_Flop d_ff_1 (.clk(or_1_out), .D(D0), .Q(out_6));  // open: Qn, preset, en, reset
  D_Flip_Flop d_ff_2 (.clk(or_1_out), .D(D1), .Q(out_7));  // open: Qn, preset, en, reset
  D_Flip_Flop d_ff_3 (.clk(or_1_out), .D(D2), .Q(out_8));  // open: Qn, preset, en, reset
  D_Flip_Flop d_ff_4 (.clk(or_1_out), .D(D3), .Q(out_9));  // open: Qn, preset, en, reset
  LED led_1 (.in(out_6));
  LED led_2 (.in(out_7));
  LED led_3 (.in(out_8));
  LED led_4 (.in(out_9));

  // Notes on the sheet:
  //   Clock
endmodule

module Parallel_Load (
  input  in_1,
  input  in_2,
  input  D1,
  input  D2,
  input  D3,
  output out_6,
  output out_7,
  output out_8,
  output out_9
);

  wire and_1_out, and_2_out, and_3_out, and_4_out, and_5_out, and_6_out, and_7_out, and_8_out, clock_1_out,
       not_1_out, or_1_out, or_2_out, or_3_out, or_4_out;

  not not_1 (not_1_out, in_1);
  Clock clock_1 (.out(clock_1_out));
  and and_1 (and_1_out, not_1_out, not_1_out, out_6);
  and and_2 (and_2_out, in_2, in_1);
  and and_3 (and_3_out, not_1_out, out_7);
  and and_4 (and_4_out, D1, in_1);
  and and_5 (and_5_out, not_1_out, out_8);
  and and_6 (and_6_out, D2, in_1);
  and and_7 (and_7_out, not_1_out, out_9);
  and and_8 (and_8_out, D3, in_1);
  or or_1 (or_1_out, and_1_out, and_2_out);
  or or_2 (or_2_out, and_3_out, and_4_out);
  or or_3 (or_3_out, and_5_out, and_6_out);
  or or_4 (or_4_out, and_7_out, and_8_out);
  D_Flip_Flop d_ff_1 (.clk(clock_1_out), .D(or_1_out), .Q(out_6));  // open: Qn, preset, en, reset
  D_Flip_Flop d_ff_2 (.clk(clock_1_out), .D(or_2_out), .Q(out_7));  // open: Qn, preset, en, reset
  D_Flip_Flop d_ff_3 (.clk(clock_1_out), .D(or_3_out), .Q(out_8));  // open: Qn, preset, en, reset
  D_Flip_Flop d_ff_4 (.clk(clock_1_out), .D(or_4_out), .Q(out_9));  // open: Qn, preset, en, reset
  LED led_1 (.in(out_6));
  LED led_2 (.in(out_7));
  LED led_3 (.in(out_8));
  LED led_4 (.in(out_9));

  // Notes on the sheet:
  //   Load
  //   D0
  //   Clock
endmodule

module Shift_Register (
  input  Shift,
  input  Load,
  input  Serial_Input,
  input  in_4,
  input  D1,
  input  in_6,
  input  D3,
  output out_8,
  output out_9,
  output out_10,
  output out_11
);

  wire and_1_out, and_2_out, and_3_out, and_4_out, and_5_out, and_6_out, and_7_out, and_8_out, and_9_out,
       and_10_out, and_11_out, and_12_out, clock_1_out, not_1_out, not_2_out, or_1_out, or_2_out, or_3_out,
       or_4_out;

  Clock clock_1 (.out(clock_1_out));
  not not_1 (not_1_out, Load);
  not not_2 (not_2_out, Shift);
  and and_1 (and_1_out, Serial_Input, Shift);
  and and_2 (and_2_out, not_2_out, in_4, Load);
  and and_3 (and_3_out, not_2_out, not_1_out, out_8);
  and and_4 (and_4_out, out_8, Shift);
  and and_5 (and_5_out, not_2_out, Load, D1);
  and and_6 (and_6_out, not_2_out, not_1_out, out_9);
  and and_7 (and_7_out, out_9, Shift);
  and and_8 (and_8_out, not_2_out, in_6, Load);
  and and_9 (and_9_out, not_2_out, not_1_out, out_10);
  and and_10 (and_10_out, out_10, Shift);
  and and_11 (and_11_out, not_2_out, Load, D3);
  and and_12 (and_12_out, not_2_out, not_1_out, out_11);
  or or_1 (or_1_out, and_1_out, and_2_out, and_3_out);
  or or_2 (or_2_out, and_4_out, and_5_out, and_6_out);
  or or_3 (or_3_out, and_7_out, and_8_out, and_9_out);
  or or_4 (or_4_out, and_10_out, and_11_out, and_12_out);
  D_Flip_Flop d_ff_1 (.clk(clock_1_out), .D(or_1_out), .Q(out_8));  // open: Qn, preset, en, reset
  D_Flip_Flop d_ff_2 (.clk(clock_1_out), .D(or_2_out), .Q(out_9));  // open: Qn, preset, en, reset
  D_Flip_Flop d_ff_3 (.clk(clock_1_out), .D(or_3_out), .Q(out_10));  // open: Qn, preset, en, reset
  D_Flip_Flop d_ff_4 (.clk(clock_1_out), .D(or_4_out), .Q(out_11));  // open: Qn, preset, en, reset

  // Notes on the sheet:
  //   D0
  //   D2
  //   Clock
endmodule

module Jk_Shift_Register (
  input  Switch,
  input  B,
  output A,
  output out_4,
  output out_5,
  output out_6,
  output out_7
);

  wire not_2_out, not_3_out, not_4_out;

  Clock clock_1 (.out(A));
  // NOT_Gate not_1 has open pins: in=Switch, out=open
  J_K_Flip_Flop j_k_ff_1 (.J(Switch), .clk(A), .K(Switch), .Q(out_4), .reset(B));  // open: Qn, preset, en
  not not_2 (not_2_out, out_4);
  J_K_Flip_Flop j_k_ff_2 (.J(out_4), .clk(A), .K(not_2_out), .Q(out_5), .reset(B));  // open: Qn, preset, en
  not not_3 (not_3_out, out_5);
  J_K_Flip_Flop j_k_ff_3 (.J(out_5), .clk(A), .K(not_3_out), .Q(out_6), .reset(B));  // open: Qn, preset, en
  not not_4 (not_4_out, out_6);
  J_K_Flip_Flop j_k_ff_4 (.J(out_6), .clk(A), .K(not_4_out), .Q(out_7), .reset(B));  // open: Qn, preset, en

  // Notes on the sheet:
  //   Clock 
endmodule

module Ripple_Counter (
  output out_1,
  output out_2,
  output out_3,
  output out_4
);

  wire and_1_out, clock_1_out;

  Clock clock_1 (.out(clock_1_out));
  J_K_Flip_Flop j_k_ff_1 (.J(1'b1), .clk(clock_1_out), .K(1'b1), .Q(out_1), .reset(and_1_out));  // open: Qn, preset, en
  J_K_Flip_Flop j_k_ff_2 (.J(1'b1), .clk(out_1), .K(1'b1), .Q(out_2), .reset(and_1_out));  // open: Qn, preset, en
  J_K_Flip_Flop j_k_ff_3 (.J(1'b1), .clk(out_2), .K(1'b1), .Q(out_3), .reset(and_1_out));  // open: Qn, preset, en
  J_K_Flip_Flop j_k_ff_4 (.J(1'b1), .clk(out_3), .K(1'b1), .Q(out_4), .reset(and_1_out));  // open: Qn, preset, en
  and and_1 (and_1_out, out_2, out_4);

  // Notes on the sheet:
  //   Clock
endmodule

module Serial_register (
  input  in_1,
  input  Shift,
  input  in_3,
  input  in_4,
  input  in_5,
  input  in_6
);

  wire adder_1_cout, adder_1_out, clock_1_out, d_ff_1_q, not_1_out, or_1_out, register_1_q,
       shift_register_1_out;

  not not_1 (not_1_out, Shift);
  Clock clock_1 (.out(clock_1_out));
  or or_1 (or_1_out, not_1_out, clock_1_out);
  Shift_Register_part #(.length(4)) shift_register_1 (
    .in(in_1), .clk(or_1_out), .out(shift_register_1_out), .clr(in_3));  // open: shift, load, d0, q0, d1, q1, d2, q2, d3, q3
  Register #(.width(1)) register_1 (.en(in_4), .Q(register_1_q), .clk(or_1_out), .clr(in_5));  // open: D
  Adder #(.width(1)) adder_1 (
    .a(shift_register_1_out), .b(register_1_q), .out(adder_1_out), .cin(d_ff_1_q), .cout(adder_1_cout));
  D_Flip_Flop d_ff_1 (.clk(or_1_out), .D(adder_1_cout), .Q(d_ff_1_q), .reset(in_6));  // open: Qn, preset, en
  Shift_Register_part #(.length(4)) shift_register_2 (
    .in(adder_1_out), .clk(or_1_out));  // open: shift, out, load, clr, d0, q0, d1, q1, d2, q2, d3, q3

  // Notes on the sheet:
  //   Clock
  //   Reset
  //   Reset
endmodule

module Serial_additon (
  input  in_1
);

  Clock clock_1 ();  // open: out
endmodule

module _8bit_synch_counter (
  input  up_down,
  input  in_2
);

  wire clock_1_out;

  Clock clock_1 (.out(clock_1_out));
  D_Flip_Flop d_ff_1 ();  // open: clk, D, Q, Qn, preset, en, reset
  Multiplexer multiplexer_1 ();  // open: in0, in1, out, sel, en
  // XOR_Gate xor_1 is placed but not wired
  D_Flip_Flop d_ff_2 ();  // open: clk, D, Q, Qn, preset, en, reset
  // AND_Gate and_1 is placed but not wired
  // AND_Gate and_2 is placed but not wired
  Multiplexer multiplexer_2 ();  // open: in0, in1, out, sel, en
  // XOR_Gate xor_2 is placed but not wired
  D_Flip_Flop d_ff_3 ();  // open: clk, D, Q, Qn, preset, en, reset
  // AND_Gate and_3 is placed but not wired
  // AND_Gate and_4 is placed but not wired
  Multiplexer multiplexer_3 ();  // open: in0, in1, out, sel, en
  // XOR_Gate xor_3 is placed but not wired
  D_Flip_Flop d_ff_4 ();  // open: clk, D, Q, Qn, preset, en, reset
endmodule
