// Logisim project lab 14.circ as structural Verilog: 2 circuits, main circuit main
module main (
);

  wire clock_1_out, j_k_ff_1_qn, j_k_ff_2_qn, j_k_ff_3_qn, j_k_ff_4_qn, n7_segment_display_1_out_5,
       n7_segment_display_1_out_6, n7_segment_display_1_out_7, n7_segment_display_1_out_8,
       n7_segment_display_1_out_9, n7_segment_display_1_out_10, n7_segment_display_1_out_11;

  Clock clock_1 (.out(clock_1_out));
  J_K_Flip_Flop j_k_ff_1 (.J(1'b1), .clk(clock_1_out), .K(1'b1), .Qn(j_k_ff_1_qn));  // open: Q, preset, en, reset
  _7_segment_display u_7_segment_display_1 (
    .in_1(j_k_ff_4_qn), .in_2(j_k_ff_3_qn), .in_3(j_k_ff_2_qn), .in_4(j_k_ff_1_qn),
    .out_5(n7_segment_display_1_out_5), .out_6(n7_segment_display_1_out_6),
    .out_7(n7_segment_display_1_out_7), .out_8(n7_segment_display_1_out_8),
    .out_9(n7_segment_display_1_out_9), .out_10(n7_segment_display_1_out_10),
    .out_11(n7_segment_display_1_out_11));
  J_K_Flip_Flop j_k_ff_2 (.J(1'b1), .clk(j_k_ff_1_qn), .K(1'b1), .Qn(j_k_ff_2_qn));  // open: Q, preset, en, reset
  _7_Segment_Display u_7_segment_display_2 (
    .g(n7_segment_display_1_out_11), .f(n7_segment_display_1_out_10), .a(n7_segment_display_1_out_5),
    .b(n7_segment_display_1_out_6), .e(n7_segment_display_1_out_9), .d(n7_segment_display_1_out_8),
    .c(n7_segment_display_1_out_7));  // open: dp
  J_K_Flip_Flop j_k_ff_3 (.J(1'b1), .clk(j_k_ff_2_qn), .K(1'b1), .Qn(j_k_ff_3_qn));  // open: Q, preset, en, reset
  J_K_Flip_Flop j_k_ff_4 (.J(1'b1), .clk(j_k_ff_3_qn), .K(1'b1), .Qn(j_k_ff_4_qn));  // open: Q, preset, en, reset
endmodule

module _7_segment_display (
  input  in_1,
  input  in_2,
  input  in_3,
  input  in_4,
  output out_5,
  output out_6,
  output out_7,
  output out_8,
  output out_9,
  output out_10,
  output out_11
);

  wire and_1_out, and_2_out, and_3_out, and_4_out, and_5_out, and_6_out, and_7_out, and_8_out, and_9_out,
       and_10_out, and_11_out, and_12_out, and_13_out, and_14_out, and_15_out, and_16_out, and_17_out,
       and_18_out, and_19_out, and_20_out, and_21_out, and_22_out, and_23_out, and_24_out, and_25_out,
       and_26_out, and_27_out, and_28_out, and_29_out, and_30_out, and_31_out, and_32_out, and_33_out,
       and_34_out, and_35_out, not_1_out, not_2_out, not_3_out, not_4_out;

  not not_1 (not_1_out, in_1);
  not not_2 (not_2_out, in_2);
  not not_3 (not_3_out, in_3);
  not not_4 (not_4_out, in_4);
  and and_1 (and_1_out, not_2_out, not_4_out);
  and and_2 (and_2_out, not_1_out, not_2_out);
  and and_3 (and_3_out, not_1_out, not_3_out);
  and and_4 (and_4_out, in_1, not_3_out);
  and and_5 (and_5_out, not_2_out, not_4_out);
  and and_6 (and_6_out, not_3_out, not_4_out, not_4_out);
  and and_7 (and_7_out, not_2_out, in_3);
  and and_8 (and_8_out, not_1_out, in_3);
  and and_9 (and_9_out, in_2, in_3);
  and and_10 (and_10_out, not_2_out, not_4_out);
  and and_11 (and_11_out, not_1_out, not_3_out, not_4_out);
  and and_12 (and_12_out, not_1_out, in_4);
  and and_13 (and_13_out, not_3_out, in_4);
  and and_14 (and_14_out, not_1_out, not_2_out, not_4_out);
  and and_15 (and_15_out, not_2_out, in_3, in_4);
  and and_16 (and_16_out, in_3, not_4_out);
  and and_17 (and_17_out, in_1, in_3);
  and and_18 (and_18_out, in_2, not_4_out);
  and and_19 (and_19_out, in_1, not_2_out);
  and and_20 (and_20_out, in_3, not_4_out);
  and and_21 (and_21_out, in_1, not_2_out);
  and and_22 (and_22_out, in_1, not_4_out);
  and and_23 (and_23_out, not_1_out, in_3, in_4);
  and and_24 (and_24_out, not_1_out, in_2);
  and and_25 (and_25_out, in_2, not_3_out, in_4);
  and and_26 (and_26_out, in_1, in_2);
  and and_27 (and_27_out, in_1, in_3);
  and and_28 (and_28_out, in_1, in_4);
  and and_29 (and_29_out, not_1_out, in_2, in_4);
  and and_30 (and_30_out, in_1, not_2_out, not_3_out);
  and and_31 (and_31_out, in_1, not_3_out, in_4);
  and and_32 (and_32_out, in_1, not_2_out);
  and and_33 (and_33_out, in_2, in_3, not_4_out);
  and and_34 (and_34_out, not_1_out, in_2, not_3_out);
  and and_35 (and_35_out, not_1_out, in_2, not_3_out);
  or A (out_5, and_1_out, and_8_out, and_9_out, and_22_out, and_29_out, and_30_out);
  or B (out_6, and_2_out, and_10_out, and_11_out, and_23_out, and_31_out);
  or C (out_7, and_3_out, and_12_out, and_13_out, and_24_out, and_32_out);
  or D (out_8, and_4_out, and_14_out, and_15_out, and_25_out, and_33_out);
  or E (out_9, and_5_out, and_16_out, and_17_out, and_26_out);
  or F (out_10, and_6_out, and_18_out, and_19_out, and_27_out, and_34_out);
  or G (out_11, and_7_out, and_20_out, and_21_out, and_28_out, and_35_out);
endmodule
