// Logisim project lab 9.circ as structural Verilog: 1 circuit, main circuit main
module main (
  input  in_1,
  input  in_2,
  input  in_3
);

  wire not_1_out, shift_register_1_out;

  Shift_Register #(.length(3)) shift_register_1 (.out(shift_register_1_out));  // open: shift, in, clk, load, clr, d0, q0, d1, q1, d2, q2
  not not_1 (not_1_out, in_1);
  Multiplexer #(.select(3)) multiplexer_1 (
    .in0(not_1_out), .in1(in_1), .in2(in_1), .in3(in_1), .in4(in_2), .in5(in_1), .in6(in_1), .in7(in_3),
    .en(shift_register_1_out));  // open: out, sel
endmodule
