// Logisim project lab13 registers.circ as structural Verilog: 9 circuits, main circuit main
module main (
  input  in_1,
  output out_2,
  output out_3
);

  wire clock_1_out;

  Clock clock_1 (.out(clock_1_out));
  D_Flip_Flop d_ff_1 (.clk(clock_1_out), .D(in_1), .Q(out_2), .Qn(out_3));  // open: preset, en, reset
  T_Flip_Flop t_ff_1 ();  // open: clk, T, Q, Qn, preset, reset, en
  Data_register data_register_1 ();  // open: do, reset, D1, D2, D3, Q0, out_7, Q1, out_9, Q2, out_11, Q3, out_13
  Register_with_parallel_load register_with_parallel_load_1 ();  // open: Load, D0, reset, D1, D2, D3, Q0, out_8, Q1, out_10, Q2, out_12, Q3, out_14
  jk_flop_register jk_flop_register_1 ();  // open: do, reset, D1, D2, D3, Q0, out_7, Q1, out_9, Q2, out_11, Q3, out_13
  J_K_Flip_Flop j_k_ff_1 ();  // open: J, clk, K, Q, Qn, preset, en, reset
  S_R_Flip_Flop s_r_ff_1 ();  // open: S, clk, R, Q, Qn, preset, reset, en
  shift_register shift_register_1 ();  // open: in_1, in_2, in_3, out_4
endmodule

module Data_register (
  input  \do ,
  input  reset,
  input  D1,
  input  D2,
  input  D3,
  output Q0,
  output out_7,
  output Q1,
  output out_9,
  output Q2,
  output out_11,
  output Q3,
  output out_13
);

  wire clock_out;

  Clock clock (.out(clock_out));
  D_Flip_Flop d_ff_1 (.clk(clock_out), .D(\do ), .Q(Q0), .Qn(out_7), .reset(reset));  // open: preset, en
  D_Flip_Flop d_ff_2 (.clk(clock_out), .D(D1), .Q(Q1), .Qn(out_9), .reset(reset));  // open: preset, en
  D_Flip_Flop d_ff_3 (.clk(clock_out), .D(D2), .Q(Q2), .Qn(out_11), .reset(reset));  // open: preset, en
  D_Flip_Flop d_ff_4 (.clk(clock_out), .D(D3), .Q(Q3), .Qn(out_13), .reset(reset));  // open: preset, en
endmodule

module Register_with_parallel_load (
  input  Load,
  input  D0,
  input  reset,
  input  D1,
  input  D2,
  input  D3,
  output Q0,
  output out_8,
  output Q1,
  output out_10,
  output Q2,
  output out_12,
  output Q3,
  output out_14
);

  wire clock_out, not_1_out, or_1_out;

  Clock clock (.out(clock_out));
  not not_1 (not_1_out, Load);
  or or_1 (or_1_out, clock_out, not_1_out);
  D_Flip_Flop d_ff_1 (.clk(or_1_out), .D(D0), .Q(Q0), .Qn(out_8), .reset(reset));  // open: preset, en
  D_Flip_Flop d_ff_2 (.clk(or_1_out), .D(D1), .Q(Q1), .Qn(out_10), .reset(reset));  // open: preset, en
  D_Flip_Flop d_ff_3 (.clk(or_1_out), .D(D2), .Q(Q2), .Qn(out_12), .reset(reset));  // open: preset, en
  D_Flip_Flop d_ff_4 (.clk(or_1_out), .D(D3), .Q(Q3), .Qn(out_14), .reset(reset));  // open: preset, en
endmodule

module jk_flop_register (
  input  \do ,
  input  reset,
  input  D1,
  input  D2,
  input  D3,
  output Q0,
  output out_7,
  output Q1,
  output out_9,
  output Q2,
  output out_11,
  output Q3,
  output out_13
);

  wire clock_out, not_1_out, not_2_out, not_3_out, not_4_out;

  Clock clock (.out(clock_out));
  not not_1 (not_1_out, \do );
  J_K_Flip_Flop j_k_ff_1 (
    .J(not_1_out), .clk(clock_out), .K(\do ), .Q(Q0), .Qn(out_7), .reset(reset));  // open: preset, en
  J_K_Flip_Flop j_k_ff_2 (
    .J(not_2_out), .clk(clock_out), .K(D1), .Q(Q1), .Qn(out_9), .reset(reset));  // open: preset, en
  not not_2 (not_2_out, D1);
  J_K_Flip_Flop j_k_ff_3 (
    .J(not_3_out), .clk(clock_out), .K(D2), .Q(Q2), .Qn(out_11), .reset(reset));  // open: preset, en
  not not_3 (not_3_out, D2);
  not not_4 (not_4_out, D3);
  J_K_Flip_Flop j_k_ff_4 (
    .J(not_4_out), .clk(clock_out), .K(D3), .Q(Q3), .Qn(out_13), .reset(reset));  // open: preset, en
endmodule

// Shift register
module shift_register (
  input  in_1,
  input  in_2,
  input  in_3,
  output out_4
);

  wire d_ff_1_q, d_ff_2_q, d_ff_3_q;

  D_Flip_Flop d_ff_1 (.clk(in_1), .D(in_2), .Q(d_ff_1_q), .reset(in_3));  // open: Qn, preset, en
  D_Flip_Flop d_ff_2 (.clk(in_1), .D(d_ff_1_q), .Q(d_ff_2_q), .reset(in_3));  // open: Qn, preset, en
  D_Flip_Flop d_ff_3 (.clk(in_1), .D(d_ff_2_q), .Q(d_ff_3_q), .reset(in_3));  // open: Qn, preset, en
  D_Flip_Flop d_ff_4 (.clk(in_1), .D(d_ff_3_q), .Q(out_4), .reset(in_3));  // open: Qn, preset, en
endmodule

module Ripple_count (
  input  in_1,
  output out_2
);

  wire clock_1_out, j_k_ff_1_q, j_k_ff_1_qn, j_k_ff_2_q, j_k_ff_2_qn, j_k_ff_3_q, j_k_ff_3_qn, not_1_out;

  Clock clock_1 (.out(clock_1_out));
  not not_1 (not_1_out, in_1);
  J_K_Flip_Flop j_k_ff_1 (
    .J(in_1), .clk(clock_1_out), .K(not_1_out), .Q(j_k_ff_1_q), .Qn(j_k_ff_1_qn));  // open: preset, en, reset
  J_K_Flip_Flop j_k_ff_2 (
    .J(j_k_ff_1_q), .clk(clock_1_out), .K(j_k_ff_1_qn), .Q(j_k_ff_2_q), .Qn(j_k_ff_2_qn));  // open: preset, en, reset
  J_K_Flip_Flop j_k_ff_3 (
    .J(j_k_ff_2_q), .clk(clock_1_out), .K(j_k_ff_2_qn), .Q(j_k_ff_3_q), .Qn(j_k_ff_3_qn));  // open: preset, en, reset
  J_K_Flip_Flop j_k_ff_4 (
    .J(j_k_ff_3_q), .clk(clock_1_out), .K(j_k_ff_3_qn), .Q(out_2));  // open: Qn, preset, en, reset
endmodule

module Question_1 (
  input  Reset,
  input  Shift,
  input  Reset_2,
  input  Serial_input,
  input  Reset_3
);

  wire Clock_out, d_ff_1_q, full_adder_1_cout, full_adder_1_s0, not_1_out, or_1_out, shift_register_1_out_4,
       shift_register_2_out_4;

  not not_1 (not_1_out, Shift);
  Clock Clock (.out(Clock_out));
  or or_1 (or_1_out, not_1_out, Clock_out);
  shift_register shift_register_1 (
    .in_1(or_1_out), .in_2(Reset), .in_3(full_adder_1_s0), .out_4(shift_register_1_out_4));
  shift_register shift_register_2 (
    .in_1(or_1_out), .in_2(Reset_2), .in_3(Serial_input), .out_4(shift_register_2_out_4));
  Full_Adder full_adder_1 (
    .Cin(shift_register_1_out_4), .A(shift_register_2_out_4), .B(d_ff_1_q), .S0(full_adder_1_s0),
    .Cout(full_adder_1_cout));
  D_Flip_Flop d_ff_1 (.clk(full_adder_1_cout), .D(or_1_out), .Q(d_ff_1_q), .Qn(Reset_3));  // open: preset, en, reset
endmodule

module Full_Adder (
  input  Cin,
  input  A,
  input  B,
  output S0,
  output Cout
);

  wire and_1_out, and_2_out, xor_1_out;

  xor xor_1 (xor_1_out, Cin, A);
  and and_1 (and_1_out, Cin, A);
  and and_2 (and_2_out, xor_1_out, B);
  xor xor_2 (S0, B, xor_1_out);
  or or_1 (Cout, and_1_out, and_2_out);
endmodule

module Question_2 (
  input  Reset,
  input  Shift,
  input  Reset_2,
  input  Serial_input,
  input  Reset_3,
  input  in_6,
  input  in_7,
  input  in_8,
  input  in_9,
  input  in_10,
  input  in_11,
  input  in_12,
  input  in_13
);

  wire clock_1_out, d_ff_1_qn, d_ff_2_q, full_adder_1_cout, full_adder_1_s0, full_adder_2_cout, not_1_out,
       or_1_out, register_1_p3, register_1_p4, undriven_2;
  wire [7:0] register_2_q;
  wire [7:1] undriven;

  not not_1 (not_1_out, Shift);
  Clock clock_1 (.out(clock_1_out));
  or or_1 (or_1_out, not_1_out, clock_1_out);
  Full_Adder full_adder_1 (.Cin(in_6), .A(in_10), .B(undriven_2), .S0(full_adder_1_s0), .Cout(full_adder_1_cout));
  // Register register_1: pin names not known; wires that end beside it: Reset, or_1_out, register_1_p3, register_1_p4
  Register register_2 (.D({undriven, Reset_2}), .en(Serial_input), .Q(register_2_q), .clr(or_1_out));  // open: clk
  D_Flip_Flop d_ff_1 (.clk(undriven_2), .Q(full_adder_1_cout), .Qn(d_ff_1_qn));  // open: D, preset, en, reset
  Clock clock_2 (.out(d_ff_1_qn));
  Full_Adder full_adder_2 (
    .Cin(register_1_p4), .A(register_2_q[0]), .B(d_ff_2_q), .S0(register_1_p3), .Cout(full_adder_2_cout));
  D_Flip_Flop d_ff_2 (.clk(full_adder_2_cout), .D(or_1_out), .Q(d_ff_2_q), .Qn(Reset_3));  // open: preset, en, reset
  // Pins of 1 and 8 bits meet at {undriven, Reset_2}
  // Pins of 1 and 8 bits meet at register_2_q

  assign in_7 = in_6;
  assign in_8 = in_6;
  assign in_9 = in_6;
  assign in_11 = in_10;
  assign in_12 = in_10;
  assign in_13 = in_10;
endmodule
