// Logisim project registers.circ as structural Verilog: 5 circuits, main circuit main
module main (
  input  in_1,
  output out_2,
  output out_3
);

  wire clock_1_out;

  Clock clock_1 (.out(clock_1_out));
  D_Flip_Flop d_ff_1 (.clk(clock_1_out), .D(in_1), .Q(out_2), .Qn(out_3));  // open: preset, en, reset
  T_Flip_Flop t_ff_1 ();  // open: clk, T, Q, Qn, preset, reset, en
  J_K_Flip_Flop j_k_ff_1 ();  // open: J, clk, K, Q, Qn, preset, en, reset
  S_R_Flip_Flop s_r_ff_1 ();  // open: S, clk, R, Q, Qn, preset, reset, en
endmodule

module Data_register (
  input  \do ,
  input  reset,
  input  D1,
  input  D2,
  input  D3,
  output Q0,
  output out_7,
  output Q1,
  output out_9,
  output Q2,
  output out_11,
  output Q3,
  output out_13
);

  wire clock_out;

  Clock clock (.out(clock_out));
  D_Flip_Flop d_ff_1 (.clk(clock_out), .D(\do ), .Q(Q0), .Qn(out_7), .reset(reset));  // open: preset, en
  D_Flip_Flop d_ff_2 (.clk(clock_out), .D(D1), .Q(Q1), .Qn(out_9), .reset(reset));  // open: preset, en
  D_Flip_Flop d_ff_3 (.clk(clock_out), .D(D2), .Q(Q2), .Qn(out_11), .reset(reset));  // open: preset, en
  D_Flip_Flop d_ff_4 (.clk(clock_out), .D(D3), .Q(Q3), .Qn(out_13), .reset(reset));  // open: preset, en
endmodule

module Register_with_parallel_load (
  input  Load,
  input  D0,
  input  reset,
  input  D1,
  input  D2,
  input  D3,
  output Q0,
  output out_8,
  output Q1,
  output out_10,
  output Q2,
  output out_12,
  output Q3,
  output out_14
);

  wire clock_out, not_1_out, or_1_out;

  Clock clock (.out(clock_out));
  not not_1 (not_1_out, Load);
  Random random_1 ();  // open: clk, next, out, clr
  Shift_Register shift_register_1 ();  // open: shift, in, clk, out, load, clr, d0, q0, d1, q1, d2, q2, d3, q3, d4, q4, d5, q5, d6, q6, d7, q7
  Register register_1 ();  // open: D, en, Q, clk, clr
  or or_1 (or_1_out, clock_out, not_1_out);
  D_Flip_Flop d_ff_1 (.clk(or_1_out), .D(D0), .Q(Q0), .Qn(out_8), .reset(reset));  // open: preset, en
  D_Flip_Flop d_ff_2 (.clk(or_1_out), .D(D1), .Q(Q1), .Qn(out_10), .reset(reset));  // open: preset, en
  D_Flip_Flop d_ff_3 (.clk(or_1_out), .D(D2), .Q(Q2), .Qn(out_12), .reset(reset));  // open: preset, en
  D_Flip_Flop d_ff_4 (.clk(or_1_out), .D(D3), .Q(Q3), .Qn(out_14), .reset(reset));  // open: preset, en
endmodule

module jk_flop_register (
  input  \do ,
  input  reset,
  input  D1,
  input  D2,
  input  D3,
  output Q0,
  output out_7,
  output Q1,
  output out_9,
  output Q2,
  output out_11,
  output Q3,
  output out_13
);

  wire clock_out, not_1_out, not_2_out, not_3_out, not_4_out;

  Clock clock (.out(clock_out));
  J_K_Flip_Flop j_k_ff_1 (
    .J(not_1_out), .clk(clock_out), .K(\do ), .Q(Q0), .Qn(out_7), .reset(reset));  // open: preset, en
  not not_1 (not_1_out, \do );
  not not_2 (not_2_out, D1);
  J_K_Flip_Flop j_k_ff_2 (
    .J(not_2_out), .clk(clock_out), .K(D1), .Q(Q1), .Qn(out_9), .reset(reset));  // open: preset, en
  not not_3 (not_3_out, D2);
  J_K_Flip_Flop j_k_ff_3 (
    .J(not_3_out), .clk(clock_out), .K(D2), .Q(Q2), .Qn(out_11), .reset(reset));  // open: preset, en
  J_K_Flip_Flop j_k_ff_4 (
    .J(not_4_out), .clk(clock_out), .K(D3), .Q(Q3), .Qn(out_13), .reset(reset));  // open: preset, en
  not not_4 (not_4_out, D3);
endmodule

module shift_register (
  input  in_1,
  input  in_2,
  input  in_3,
  output out_4,
  output out_5
);

  wire clock_1_out, clock_2_out, d_ff_1_q, d_ff_2_q, d_ff_3_q, j_k_ff_1_q, j_k_ff_1_qn, j_k_ff_2_q,
       j_k_ff_2_qn, j_k_ff_3_q, j_k_ff_3_qn, not_1_out;

  Clock clock_1 (.out(clock_1_out));
  Clock clock_2 (.out(clock_2_out));
  not not_1 (not_1_out, in_3);
  D_Flip_Flop d_ff_1 (.clk(clock_1_out), .D(in_1), .Q(d_ff_1_q), .reset(in_2));  // open: Qn, preset, en
  J_K_Flip_Flop j_k_ff_1 (
    .J(in_3), .clk(clock_2_out), .K(not_1_out), .Q(j_k_ff_1_q), .Qn(j_k_ff_1_qn));  // open: preset, en, reset
  D_Flip_Flop d_ff_2 (.clk(clock_1_out), .D(d_ff_1_q), .Q(d_ff_2_q), .reset(in_2));  // open: Qn, preset, en
  J_K_Flip_Flop j_k_ff_2 (
    .J(j_k_ff_1_q), .clk(clock_2_out), .K(j_k_ff_1_qn), .Q(j_k_ff_2_q), .Qn(j_k_ff_2_qn));  // open: preset, en, reset
  D_Flip_Flop d_ff_3 (.clk(clock_1_out), .D(d_ff_2_q), .Q(d_ff_3_q), .reset(in_2));  // open: Qn, preset, en
  J_K_Flip_Flop j_k_ff_3 (
    .J(j_k_ff_2_q), .clk(clock_2_out), .K(j_k_ff_2_qn), .Q(j_k_ff_3_q), .Qn(j_k_ff_3_qn));  // open: preset, en, reset
  D_Flip_Flop d_ff_4 (.clk(clock_1_out), .D(d_ff_3_q), .Q(out_4), .reset(in_2));  // open: Qn, preset, en
  J_K_Flip_Flop j_k_ff_4 (
    .J(j_k_ff_3_q), .clk(clock_2_out), .K(j_k_ff_3_qn), .Q(out_5));  // open: Qn, preset, en, reset
endmodule
